// Logisim project 658_Computer.circ as structural Verilog: 2 circuits, main circuit Microcontroller
module Microcontroller (
);

  wire A_128K_B, and_1_out, and_3_out, and_6_out, and_7_out, and_8_out, BA0_3_LOW, BA4_7_LOW, clock_2_out,
       DEVICE, ds1813_1_p2, IRAM_ENABLE_B, IRQ_B, IRQ_VECTORING, lvc16373_1_p4, NMI_B, not_1_out, not_2_out,
       not_3_out, not_4_out, not_5_out, not_6_out, not_7_out, not_8_out, not_9_out, not_10_out, not_11_out,
       not_12_out, not_13_out, not_17_out, or_1_out, PHI2, pull_resistor_1_node, pull_resistor_4_node,
       pull_resistor_5_node, pull_resistor_7_node, pull_resistor_9_node, RWB, VALID_ADDRESS_B, VDA, VP_B,
       VPA, w65c816_1_p7, w65c816_1_p11;
  wire [2:0] ls148_1_p3;
  wire [3:0] A0_3;
  wire [4:0] pull_resistor_3_node;
  wire [7:0] A8_15, BA0_7, D, IRAM_A0_7;
  wire [7:4] A0_7;
  wire [7:7] pull_resistor_8_node;

  Clock clock_1 (.out(PHI2));
  Clock clock_2 (.out(clock_2_out));
  // DS1813 ds1813_1: pin names not known; wires that end beside it: clock_2_out, ds1813_1_p2
  nor nor_1 (VALID_ADDRESS_B, VDA, VPA);
  not not_1 (not_1_out, BA0_7[0]);
  not not_2 (not_2_out, BA0_7[1]);
  not not_3 (not_3_out, BA0_7[2]);
  not not_4 (not_4_out, BA0_7[3]);
  not not_5 (not_5_out, BA0_7[4]);
  not not_6 (not_6_out, BA0_7[5]);
  not not_7 (not_7_out, BA0_7[6]);
  not not_8 (not_8_out, BA0_7[7]);
  and and_1 (and_1_out, A8_15[4], A8_15[5], A8_15[6], A8_15[7]);
  Pull_Resistor #(.pull(1)) pull_resistor_1 (.node(pull_resistor_1_node));
  and and_2 (DEVICE, ~A8_15[3], and_1_out, BA0_3_LOW, BA4_7_LOW);  // AND_Gate
  and and_3 (and_3_out, not_2_out, not_3_out, not_4_out);
  and and_4 (BA0_3_LOW, not_1_out, not_2_out, not_3_out, not_4_out);
  and and_5 (BA4_7_LOW, not_5_out, not_6_out, not_7_out, not_8_out);
  and and_6 (and_6_out, A0_7[4], A0_7[5], A0_7[6]);
  and and_7 (and_7_out, A0_7[7], A8_15[0], A8_15[1], A8_15[2]);
  // W65C816 w65c816_1: pin names not known; wires that end beside it: pull_resistor_1_node, IRQ_B, NMI_B, ds1813_1_p2, PHI2, {A8_15, A0_7, A0_3}, w65c816_1_p7, RWB, VDA, VPA, w65c816_1_p11, VP_B
  nand nand_1 (A_128K_B, and_3_out, BA4_7_LOW);
  // NAND_Gate nand_2 has open pins: in0=and_6_out, in1=and_7_out, out=open
  // LVC16373 lvc16373_1: pin names not known; wires that end beside it: D, A0_3[0], A0_3[1], lvc16373_1_p4, A0_3[0], lvc16373_1_p4, A0_3[1], lvc16373_1_p4, lvc16373_1_p4
  // Probe on {A8_15, A0_7, A0_3}
  // Probe on w65c816_1_p7
  Pull_Resistor #(.pull(1)) pull_resistor_2 (.node(w65c816_1_p11));
  or or_1 (or_1_out, VALID_ADDRESS_B, DEVICE, A_128K_B);
  not not_9 (not_9_out, PHI2);
  not not_10 (not_10_out, DEVICE);
  Pull_Resistor pull_resistor_3 (.node(pull_resistor_3_node));
  or or_2 (IRAM_ENABLE_B, or_1_out, not_9_out);
  Pull_Resistor pull_resistor_4 (.node(pull_resistor_4_node));
  not not_11 (not_11_out, PHI2);
  not not_12 (not_12_out, PHI2);
  // LVC573 lvc573_1: pin names not known; wires that end beside it: pull_resistor_4_node, w65c816_1_p7, not_11_out, BA0_7
  // LVC4245 lvc4245_1: pin names not known; wires that end beside it: not_10_out, not_12_out, w65c816_1_p7, RWB, D
  Pull_Resistor pull_resistor_5 (.node(pull_resistor_5_node));
  // LVC4245 lvc4245_2: pin names not known; wires that end beside it: IRQ_VECTORING, {A0_7, A0_3}, pull_resistor_5_node, IRAM_A0_7
  // Probe on BA0_7
  // Probe on D
  Pull_Resistor #(.pull(1)) pull_resistor_6 (.node(NMI_B));
  not not_13 (not_13_out, RWB);
  Pull_Resistor pull_resistor_7 (.node(pull_resistor_7_node));
  // Probe on {BA0_7[0], A8_15, IRAM_A0_7}
  RAM #(.addrWidth(17), .databus("bidir"), .enables("line"), .trigger("high"), .\type ("nonvolatile")) ram_1 (
    .addr({BA0_7[0], A8_15, IRAM_A0_7}), .data(D));  // open: we, oe, clk
  // NOT_Gate not_14 has open pins: in=not_13_out, out=open
  // NOT_Gate not_15 has open pins: in=RWB, out=open
  // NOT_Gate not_16 has open pins: in=IRAM_ENABLE_B, out=open
  // LS148 ls148_1: pin names not known; wires that end beside it: pull_resistor_7_node, {8{1'b1}}, ls148_1_p3, IRQ_B
  Pull_Resistor pull_resistor_8 (.node(pull_resistor_8_node[7]));
  and and_8 (and_8_out, A0_3[1], A0_3[2], A0_3[3], ~VP_B);  // AND_Gate
  not not_17 (not_17_out, IRQ_VECTORING);
  // Probe on {{4{pull_resistor_8_node[7]}}, ls148_1_p3, A0_3[0]}
  and and_9 (IRQ_VECTORING, and_8_out, ~IRQ_B);  // AND_Gate
  // Probe on D
  Pull_Resistor pull_resistor_9 (.node(pull_resistor_9_node));
  // LVC4245 lvc4245_3: pin names not known; wires that end beside it: not_17_out, {{4{pull_resistor_8_node[7]}}, ls148_1_p3, A0_3[0]}, pull_resistor_9_node, IRAM_A0_7
  // Probe on IRAM_A0_7

  // Other names for the same wires on the sheet: A0_7[3:0] = A0_3; DEVICE_A0_3[3:0] = A0_3;
  //   DEVICE_N0_6[6:0] = {A8_15[2:0], A0_7}; IRAM_A8_16[7:0] = A8_15; IRAM_A17 = BA0_7[0]; A4_7[3:0] = A0_7

  // Notes on the sheet:
  //   Valid Address
  //   Bank Decode
  //   Device Decode
endmodule

module Timing_Circuit (
  output [8:0] CHANNEL,
  output RST,
  output RST_1,
  output CLK,
  output CLK_B
);

  wire and_1_out, and_2_out, clock_1_out, digital_oscilloscope_1_p11, nand_1_out, nand_2_out,
       pull_resistor_1_node, pull_resistor_2_node, pull_resistor_3_node, pull_resistor_4_node,
       pull_resistor_5_node, pull_resistor_6_node, pull_resistor_7_node, pull_resistor_8_node;
  wire [3:0] lvc163_1_p7, lvc163_2_p7;
  wire [7:4] lvc138_1_p5;
  wire [7:5] lvc138_2_p5;

  Clock clock_1 (.out(clock_1_out));
  Clock clock_2 (.out(CLK));
  // DS1813 ds1813_1: pin names not known; wires that end beside it: clock_1_out, RST
  not not_1 (CLK_B, CLK);
  D_Flip_Flop d_ff_1 (.clk(CLK), .D(RST), .Q(RST_1));  // open: Qn, preset, reset
  and and_1 (and_1_out, RST, nand_1_out);
  Pull_Resistor #(.pull(1)) pull_resistor_1 (.node(pull_resistor_1_node));
  Pull_Resistor #(.pull(1)) pull_resistor_2 (.node(pull_resistor_2_node));
  Pull_Resistor #(.pull(1)) pull_resistor_3 (.node(pull_resistor_3_node));
  and and_2 (and_2_out, RST, nand_2_out);
  Pull_Resistor #(.pull(1)) pull_resistor_4 (.node(pull_resistor_4_node));
  Pull_Resistor #(.pull(1)) pull_resistor_5 (.node(pull_resistor_5_node));
  Pull_Resistor #(.pull(1)) pull_resistor_6 (.node(pull_resistor_6_node));
  // LVC163 lvc163_1: pin names not known; wires that end beside it: and_1_out, pull_resistor_1_node, pull_resistor_2_node, CLK_B, pull_resistor_3_node, RST_1, lvc163_1_p7
  // LVC163 lvc163_2: pin names not known; wires that end beside it: and_2_out, pull_resistor_4_node, pull_resistor_5_node, CLK, pull_resistor_6_node, RST_1, lvc163_2_p7
  nand nand_1 (nand_1_out, ~lvc163_1_p7[0], ~lvc163_1_p7[1], lvc163_1_p7[2], ~lvc163_1_p7[3]);  // NAND_Gate
  nand nand_2 (nand_2_out, ~lvc163_2_p7[0], ~lvc163_2_p7[1], lvc163_2_p7[2], ~lvc163_2_p7[3]);  // NAND_Gate
  Pull_Resistor pull_resistor_7 (.node(pull_resistor_7_node));
  Pull_Resistor pull_resistor_8 (.node(pull_resistor_8_node));
  // LVC138 lvc138_1: pin names not known; wires that end beside it: pull_resistor_7_node, pull_resistor_7_node, lvc163_1_p7[2:0], RST, {lvc138_1_p5, CHANNEL[6], CHANNEL[4], CHANNEL[2], CHANNEL[0]}
  // LVC138 lvc138_2: pin names not known; wires that end beside it: pull_resistor_8_node, pull_resistor_8_node, lvc163_2_p7[2:0], RST_1, {lvc138_2_p5, CHANNEL[7], CHANNEL[5], CHANNEL[3], CHANNEL[1], CHANNEL[8]}
  Pull_Resistor #(.pull(1)) pull_resistor_9 (.node(lvc138_1_p5[4]));
  Pull_Resistor #(.pull(1)) pull_resistor_10 (.node(lvc138_1_p5[5]));
  Pull_Resistor #(.pull(1)) pull_resistor_11 (.node(lvc138_1_p5[6]));
  Pull_Resistor #(.pull(1)) pull_resistor_12 (.node(lvc138_1_p5[7]));
  Pull_Resistor #(.pull(1)) pull_resistor_13 (.node(lvc138_2_p5[5]));
  Pull_Resistor #(.pull(1)) pull_resistor_14 (.node(lvc138_2_p5[6]));
  Pull_Resistor #(.pull(1)) pull_resistor_15 (.node(lvc138_2_p5[7]));
  // Digital_Oscilloscope #(.nState(16)) digital_oscilloscope_1: pin names not known; wires that end beside it: CLK, CHANNEL[0], CHANNEL[1], CHANNEL[2], CHANNEL[3], CHANNEL[4], CHANNEL[5], CHANNEL[6], CHANNEL[7], CHANNEL[8], digital_oscilloscope_1_p11
  Clock clock_3 (.out(digital_oscilloscope_1_p11));

  // Other names for the same wires on the sheet: CLOCK = CLK; CLOCK_B = CLK_B; RESET_0 = RST; RESET_1 = RST_1
endmodule
